# Fritzing sketch pewpew-10.3 (saved by Fritzing 0.9.3b)
circuit board: 10cm x 7.50001cm
breadboards: 1

parts:
  ATSAMD21E18A-MU = QFN-32 [chip_label=SAMD21 package=QFN]
  X1a = mystery part, 8 pins [chip_label="LED Matrix"]
  X1b = mystery part, 8 pins [chip_label="LED Matrix"]
  10118193-0001LF = USB Connectors [package=usb-microb]
  1µF = Ceramic Capacitor [capacitance=1µF package="0603 [SMD, multilayer]"]
  1µF_2 = Ceramic Capacitor [capacitance=1µF package="0603 [SMD, multilayer]"]
  Pad1 = Pad [width=2.6000000000000001 height=2.6000000000000001 connect=center]
  ↑ = SKPMAPE010 [package=SKPMAPE010]
  ↓ = SKPMAPE010 [package=SKPMAPE010]
  ← = SKPMAPE010 [package=SKPMAPE010]
  → = SKPMAPE010 [package=SKPMAPE010]
  o = SKPMAPE010 [package=SKPMAPE010]
  x = SKPMAPE010 [package=SKPMAPE010]
  0N_0FF = SPST Switch [package=switch-spdt_lock.007s]
  J1 = female alternating pin header, 12 pins [form="♀ (female)"]
  J2 = female pin header, 8 pins [form="♀ (female)"]  # not connected
  J3 = female pin header, 8 pins [form="♀ (female)"]  # not connected
  J4 = female pin header, 8 pins [form="♀ (female)"]  # not connected
  J5 = female pin header, 8 pins [form="♀ (female)"]  # not connected
  J6 = female pin header, 8 pins [form="♀ (female)"]  # not connected
  J7 = female pin header, 8 pins [form="♀ (female)"]  # not connected
  J8 = female pin header, 8 pins [form="♀ (female)"]  # not connected
  J9 = female pin header, 8 pins [form="♀ (female)"]  # not connected
  J10 = female pin header, 8 pins [form="♀ (female)"]  # not connected
  J11 = female pin header, 8 pins [form="♀ (female)"]  # not connected
  J12 = female pin header, 8 pins [form="♀ (female)"]  # not connected
  J13 = female pin header, 8 pins [form="♀ (female)"]  # not connected
  J14 = female pin header, 8 pins [form="♀ (female)"]  # not connected
  J15 = female pin header, 8 pins [form="♀ (female)"]  # not connected
  + = female pin header, 1 pin [form="♀ (female)"]
  - = female pin header, 1 pin [form="♀ (female)"]

nets:
  N1: ATSAMD21E18A-MU.1, J1.pin6
  N2: ATSAMD21E18A-MU.2, J1.pin7
  N3: ATSAMD21E18A-MU.3, J1.pin8
  N4: ATSAMD21E18A-MU.4, J1.pin9
  N5: ATSAMD21E18A-MU.5, J1.pin10
  R1: ATSAMD21E18A-MU.6, X1b.pin8
  C4: ATSAMD21E18A-MU.7, X1b.pin7
  C6: ATSAMD21E18A-MU.8, X1b.pin6, ↑.2
  3.3V: ATSAMD21E18A-MU.9, ATSAMD21E18A-MU.30, 1µF.0, 0N_0FF.P, 0N_0FF.S, J1.pin11, J1.pin12
  GND: ATSAMD21E18A-MU.10, ATSAMD21E18A-MU.28, 10118193-0001LF.GND, 1µF.1, 1µF_2.1, Pad1.pad, J1.pin2, J1.pin3, -.pin1
  BUTTONS: ATSAMD21E18A-MU.11, ↑.1, ↓.2, ←.1, →.1, o.2, x.2
  R4: ATSAMD21E18A-MU.12, X1b.pin5
  C1: ATSAMD21E18A-MU.13, X1b.pin4, →.2
  R2: ATSAMD21E18A-MU.14, X1b.pin3
  C7: ATSAMD21E18A-MU.15, X1b.pin2, ←.2
  C8: ATSAMD21E18A-MU.16, X1b.pin1, ↓.1
  R5: ATSAMD21E18A-MU.17, X1a.pin1
  R7: ATSAMD21E18A-MU.18, X1a.pin2
  C2: ATSAMD21E18A-MU.19, X1a.pin3, x.1
  C3: ATSAMD21E18A-MU.20, X1a.pin4, o.1
  R8: ATSAMD21E18A-MU.21, X1a.pin5
  C5: ATSAMD21E18A-MU.22, X1a.pin6
  N6: ATSAMD21E18A-MU.23, 10118193-0001LF.D-
  N7: ATSAMD21E18A-MU.24, 10118193-0001LF.D+
  R6: ATSAMD21E18A-MU.25, X1a.pin7
  RST: ATSAMD21E18A-MU.26, J1.pin1
  R3: ATSAMD21E18A-MU.27, X1a.pin8
  N8: ATSAMD21E18A-MU.29, 1µF_2.0
  SWC: ATSAMD21E18A-MU.31, J1.pin4
  SWD: ATSAMD21E18A-MU.32, J1.pin5
  N9: 0N_0FF.O, +.pin1

notes:
  1
  R - - 1 2 3 4 5 6 7 + +3V
  Pew
  v10.3
  KYX-2588BX

custom parts:
  SKPMAPE010: Various NO switches- pushbuttons, reed, etc
